// Digital circuit cicuit copy.dig as structural Verilog
module cicuit_copy (
  input  in_1
);

  wire not_1_out, not_2_out, not_3_out, u_CONTROLL_alu_in_src, u_CONTROLL_branch, u_CONTROLL_mem_read,
       u_CONTROLL_mem_to_reg, u_CONTROLL_mem_write, u_CONTROLL_pc_reg_to_ula, u_CONTROLL_reg_write, u_ULA_z;
  wire [3:0] add_1_s, add_2_s, multiplexer_1_out, register_1_q, u_CONTROLL_alu_op, u_INST_DECODER_op_code,
       u_INST_DECODER_out_imm4, u_INST_DECODER_out_rd, u_INST_DECODER_out_rs1, u_INST_DECODER_out_rs2;
  wire [7:0] u_INST_DECODER_out_imm8;
  wire [15:0] Data_Ram_d, Instruction_Ram_d, multiplexer_2_out, multiplexer_3_out, multiplexer_4_out,
       registerfile_1_da, registerfile_1_db, u_IMMCONV_4to16_out_imm16, u_IMMGEN_out_imm8, u_ULA_s;

  Register #(.Bits(4)) register_1 (.D(multiplexer_1_out), .C(in_1), .en(1'b1), .Q(register_1_q));
  // Probe on register_1_q
  Multiplexer #(.Bits(4)) multiplexer_1 (
    .sel(u_CONTROLL_branch), .in_0(add_1_s), .in_1(add_2_s), .out(multiplexer_1_out));
  not not_1 (not_1_out, in_1);
  RAMDualPort #(.AddrBits(4), .Bits(16)) Instruction_Ram (
    .A(register_1_q), .Din({16{1'b0}}), .str(1'b0), .C(not_1_out), .ld(1'b1), .D(Instruction_Ram_d));
  Add #(.Bits(4)) add_1 (.a(register_1_q), .b(4'b0001), .c_i(1'b0), .s(add_1_s));  // open: c_o
  IMMCONV_4to16 #(.applicationType("GHDL"), .CodeFile("D:\\github\\uffs-arquivos\\SEM4\\org\\proc18bits\\immconv_4to16.vhd")) u_IMMCONV_4to16 (
    .imm4(register_1_q), .out_imm16(u_IMMCONV_4to16_out_imm16));
  // Probe on Instruction_Ram_d
  INST_DECODER #(.applicationType("GHDL"), .CodeFile("D:\\github\\uffs-arquivos\\SEM4\\org\\proc18bits\\instruction_decoder.vhd")) u_INST_DECODER (
    .inst(Instruction_Ram_d), .op_code(u_INST_DECODER_op_code), .out_rd(u_INST_DECODER_out_rd),
    .out_rs1(u_INST_DECODER_out_rs1), .out_rs2(u_INST_DECODER_out_rs2), .out_imm4(u_INST_DECODER_out_imm4),
    .out_imm8(u_INST_DECODER_out_imm8));
  // Probe on u_INST_DECODER_op_code
  CONTROLL #(.applicationType("GHDL"), .CodeFile("D:\\github\\uffs-arquivos\\SEM4\\org\\proc18bits\\controll.vhd")) u_CONTROLL (
    .inst(u_INST_DECODER_op_code), .zero(u_ULA_z), .branch(u_CONTROLL_branch),
    .mem_write(u_CONTROLL_mem_write), .mem_read(u_CONTROLL_mem_read), .mem_to_reg(u_CONTROLL_mem_to_reg),
    .alu_op(u_CONTROLL_alu_op), .alu_in_src(u_CONTROLL_alu_in_src), .reg_write(u_CONTROLL_reg_write),
    .pc_reg_to_ula(u_CONTROLL_pc_reg_to_ula));
  // Probe on u_INST_DECODER_out_rd
  not not_2 (not_2_out, in_1);
  RegisterFile #(.AddrBits(4), .Bits(16)) registerfile_1 (
    .Din(multiplexer_4_out), .we(u_CONTROLL_reg_write), .Rw(u_INST_DECODER_out_rd), .C(not_2_out),
    .Ra(u_INST_DECODER_out_rs1), .Rb(u_INST_DECODER_out_rs2), .Da(registerfile_1_da), .Db(registerfile_1_db));
  // Probe on u_INST_DECODER_out_rs1
  // Probe on u_INST_DECODER_out_rs2
  IMMGEN #(.applicationType("GHDL"), .CodeFile("D:\\github\\uffs-arquivos\\SEM4\\org\\proc18bits\\imm_gen.vhd")) u_IMMGEN (
    .imm8(u_INST_DECODER_out_imm8), .out_imm8(u_IMMGEN_out_imm8));
  Add #(.Bits(4)) add_2 (.a(register_1_q), .b(u_INST_DECODER_out_imm4), .c_i(1'b0), .s(add_2_s));  // open: c_o
  Multiplexer #(.Bits(16)) multiplexer_2 (
    .sel(u_CONTROLL_pc_reg_to_ula), .in_0(u_IMMCONV_4to16_out_imm16), .in_1(registerfile_1_da),
    .out(multiplexer_2_out));
  // Probe on u_INST_DECODER_out_imm4
  // Probe on registerfile_1_db
  Multiplexer #(.Bits(16)) multiplexer_3 (
    .sel(u_CONTROLL_alu_in_src), .in_0(registerfile_1_db), .in_1(u_IMMGEN_out_imm8), .out(multiplexer_3_out));
  // Probe on u_IMMGEN_out_imm8
  // Probe on u_CONTROLL_alu_op
  // Probe on multiplexer_2_out
  ULA #(.applicationType("GHDL"), .CodeFile("D:\\github\\uffs-arquivos\\SEM4\\org\\proc18bits\\ula.vhd")) u_ULA (
    .op(u_CONTROLL_alu_op), .a(multiplexer_2_out), .b(multiplexer_3_out), .z(u_ULA_z), .s(u_ULA_s));
  // Probe on multiplexer_3_out
  not not_3 (not_3_out, in_1);
  // Probe on u_ULA_s
  RAMDualPort #(.AddrBits(16), .Bits(16)) Data_Ram (
    .A(u_ULA_s), .Din(multiplexer_2_out), .str(u_CONTROLL_mem_write), .C(not_3_out),
    .ld(u_CONTROLL_mem_read), .D(Data_Ram_d));
  // Probe on u_ULA_s
  Multiplexer #(.Bits(16)) multiplexer_4 (
    .sel(u_CONTROLL_mem_to_reg), .in_0(Data_Ram_d), .in_1(u_ULA_s), .out(multiplexer_4_out));
  // Probe on u_CONTROLL_mem_to_reg
  // Probe on multiplexer_4_out
endmodule
