// Digital circuit cicuit.dig as structural Verilog
module cicuit (
  input  clk,
  input  in_2
);

  wire and_1_out, not_1_out, not_2_out, not_3_out, u_CONTROLL_alu_in_src, u_CONTROLL_branch,
       u_CONTROLL_compare_instruct_controll, u_CONTROLL_mem_read, u_CONTROLL_mem_to_reg,
       u_CONTROLL_mem_write, u_CONTROLL_reg_write, u_ULA_bge, u_ULA_blt, u_ULA_z;
  wire [3:0] multiplexer_2_out, multiplexer_3_out, u_CONTROLL_alu_op, u_INST_DECODER_op_code,
       u_INST_DECODER_out_rd, u_INST_DECODER_out_rs1, u_INST_DECODER_out_rs2;
  wire [7:0] add_1_s, add_2_s, multiplexer_1_out, register_1_q, u_INST_DECODER_out_imm8;
  wire [15:0] Data_Ram_d, Instruction_Ram_d, multiplexer_4_out, multiplexer_5_out, registerfile_1_da,
       registerfile_1_db, u_IMMGEN_out_imm8, u_ULA_s;

  and and_1 (and_1_out, clk, in_2);
  // Probe on multiplexer_1_out
  Register #(.Bits(8)) register_1 (.D(multiplexer_1_out), .C(and_1_out), .en(1'b1), .Q(register_1_q));
  // Probe on register_1_q
  Multiplexer #(.Bits(8)) multiplexer_1 (
    .sel(u_CONTROLL_branch), .in_0(add_1_s), .in_1(add_2_s), .out(multiplexer_1_out));
  RAMDualPort #(.AddrBits(8), .isProgramMemory("true"), .Bits(16)) Instruction_Ram (
    .A(register_1_q), .Din({16{1'b0}}), .str(1'b0), .C(not_1_out), .ld(1'b1), .D(Instruction_Ram_d));
  not not_1 (not_1_out, and_1_out);
  // Probe on Instruction_Ram_d
  Add #(.Bits(8)) add_1 (.a(register_1_q), .b(8'h1), .c_i(1'b0), .s(add_1_s));  // open: c_o
  INST_DECODER #(.applicationType("GHDL"), .CodeFile("D:\\github\\uffs-arquivos\\SEM4\\org\\proc18bits\\instruction_decoder.vhd")) u_INST_DECODER (
    .inst(Instruction_Ram_d), .op_code(u_INST_DECODER_op_code), .out_rd(u_INST_DECODER_out_rd),
    .out_rs1(u_INST_DECODER_out_rs1), .out_rs2(u_INST_DECODER_out_rs2), .out_imm8(u_INST_DECODER_out_imm8));  // open: out_imm4
  // Probe on u_INST_DECODER_op_code
  Multiplexer #(.Bits(4)) multiplexer_2 (
    .sel(u_CONTROLL_compare_instruct_controll), .in_0(u_INST_DECODER_out_rs1), .in_1(4'b0000),
    .out(multiplexer_2_out));
  Multiplexer #(.Bits(4)) multiplexer_3 (
    .sel(u_CONTROLL_compare_instruct_controll), .in_0(u_INST_DECODER_out_rs2), .in_1(4'b0001),
    .out(multiplexer_3_out));
  CONTROLL #(.applicationType("GHDL"), .CodeFile("D:\\github\\uffs-arquivos\\SEM4\\org\\proc18bits\\controll.vhd")) u_CONTROLL (
    .inst(u_INST_DECODER_op_code), .zero(u_ULA_z), .bge(u_ULA_bge), .blt(u_ULA_blt),
    .branch(u_CONTROLL_branch), .mem_write(u_CONTROLL_mem_write), .mem_read(u_CONTROLL_mem_read),
    .mem_to_reg(u_CONTROLL_mem_to_reg), .alu_op(u_CONTROLL_alu_op), .alu_in_src(u_CONTROLL_alu_in_src),
    .reg_write(u_CONTROLL_reg_write), .compare_instruct_controll(u_CONTROLL_compare_instruct_controll));  // open: pc_reg_to_ula
  not not_2 (not_2_out, and_1_out);
  RegisterFile #(.AddrBits(4), .Bits(16)) registerfile_1 (
    .Din(multiplexer_5_out), .we(u_CONTROLL_reg_write), .Rw(u_INST_DECODER_out_rd), .C(not_2_out),
    .Ra(multiplexer_2_out), .Rb(multiplexer_3_out), .Da(registerfile_1_da), .Db(registerfile_1_db));
  // Probe on u_INST_DECODER_out_rd
  // Probe on multiplexer_2_out
  // Probe on multiplexer_3_out
  IMMGEN #(.applicationType("GHDL"), .CodeFile("D:\\github\\uffs-arquivos\\SEM4\\org\\proc18bits\\imm_gen.vhd")) u_IMMGEN (
    .imm8(u_INST_DECODER_out_imm8), .out_imm8(u_IMMGEN_out_imm8));
  Add #(.Bits(8)) add_2 (.a(register_1_q), .b(u_INST_DECODER_out_imm8), .c_i(1'b0), .s(add_2_s));  // open: c_o
  // Probe on registerfile_1_db
  Multiplexer #(.Bits(16)) multiplexer_4 (
    .sel(u_CONTROLL_alu_in_src), .in_0(registerfile_1_db), .in_1(u_IMMGEN_out_imm8), .out(multiplexer_4_out));
  // Probe on u_IMMGEN_out_imm8
  // Probe on u_CONTROLL_alu_op
  ULA #(.applicationType("GHDL"), .CodeFile("D:\\github\\uffs-arquivos\\SEM4\\org\\proc18bits\\ula.vhd")) u_ULA (
    .op(u_CONTROLL_alu_op), .a(registerfile_1_da), .b(multiplexer_4_out), .z(u_ULA_z), .bge(u_ULA_bge),
    .blt(u_ULA_blt), .s(u_ULA_s));
  // Probe on multiplexer_4_out
  // Probe on u_ULA_s
  RAMDualPort #(.AddrBits(16), .Bits(16)) Data_Ram (
    .A(u_ULA_s), .Din(registerfile_1_da), .str(u_CONTROLL_mem_write), .C(not_3_out),
    .ld(u_CONTROLL_mem_read), .D(Data_Ram_d));
  not not_3 (not_3_out, and_1_out);
  // Probe on u_ULA_s
  Multiplexer #(.Bits(16)) multiplexer_5 (
    .sel(u_CONTROLL_mem_to_reg), .in_0(Data_Ram_d), .in_1(u_ULA_s), .out(multiplexer_5_out));
  // Probe on u_CONTROLL_mem_to_reg
  // Probe on multiplexer_5_out

  // Notes on the sheet:
  //   clk: Hz: 10
endmodule
