// Digital circuit testes.dig as structural Verilog
module testes (
  input  in_1
);

  wire not_1_out;
  wire [3:0] u_INST_DECODER_op_code;
  wire [15:0] add_1_s, ramdualport_1_d, register_1_q;

  Register #(.Bits(16)) register_1 (.D(add_1_s), .C(in_1), .en(1'b1), .Q(register_1_q));
  INST_DECODER #(.applicationType("GHDL"), .CodeFile("D:\\github\\uffs-arquivos\\SEM4\\org\\proc18bits\\instruction_decoder.vhd")) u_INST_DECODER (
    .instruct(register_1_q), .op_code(u_INST_DECODER_op_code));
  // Probe on register_1_q
  Add #(.Bits(16)) add_1 (.a(register_1_q), .b(16'h1), .c_i(1'b0), .s(add_1_s));  // open: c_o
  not not_1 (not_1_out, in_1);
  RAMDualPort #(.AddrBits(4), .Bits(16)) ramdualport_1 (
    .A(u_INST_DECODER_op_code), .Din({16{1'b0}}), .str(1'b0), .C(not_1_out), .ld(1'b1), .D(ramdualport_1_d));
  // Probe on ramdualport_1_d
  INST_DECODER #(.applicationType("GHDL"), .CodeFile("D:\\github\\uffs-arquivos\\SEM4\\org\\proc18bits\\instruction_decoder.vhd")) u_INST_DECODER_2 ();  // open: instruct, op_code
  Controll u_Controll ();  // open: in, out
  RegisterFile registerfile_1 ();  // open: Din, we, Rw, C, Ra, Rb, Da, Db
  imm_gen u_imm_gen ();  // open: in, out
  RAMDualPort Data_Ram ();  // open: A, Din, str, C, ld, D
endmodule
